// Logisim project control-logic.circ as structural Verilog: 1 circuit, main circuit control_logic
module control_logic (
  input  [31:0] Instruction,
  input  BrEq,
  input  BrLt,
  output PCSel,
  output RegWEn,
  output [2:0] ImmSel,
  output BrUn,
  output ASel,
  output BSel,
  output [3:0] ALUSel,
  output MemWEn,
  output [1:0] WBSel
);

  wire and_2_out, and_4_out, and_5_out, and_6_out, and_7_out, and_14_out, and_15_out, and_16_out, and_17_out,
       and_18_out, and_19_out, and_28_out, and_30_out, and_32_out, and_34_out, and_36_out, and_37_out,
       and_38_out, and_39_out, and_40_out, and_41_out, comparator_1_eq, comparator_2_eq, comparator_3_eq,
       comparator_4_eq, comparator_5_eq, comparator_6_eq, comparator_7_eq, comparator_8_eq, comparator_9_eq,
       comparator_10_eq, comparator_11_eq, comparator_12_eq, comparator_13_eq, comparator_14_eq,
       comparator_15_eq, comparator_16_eq, comparator_17_eq, comparator_18_eq, comparator_19_eq,
       comparator_20_eq, comparator_21_eq, comparator_22_eq, comparator_23_eq, comparator_24_eq,
       comparator_25_eq, comparator_26_eq, comparator_27_eq, comparator_28_eq, comparator_29_eq,
       comparator_30_eq, comparator_31_eq, comparator_32_eq, comparator_33_eq, comparator_34_eq,
       comparator_35_eq, comparator_36_eq, comparator_37_eq, comparator_38_eq, comparator_39_eq,
       comparator_40_eq, comparator_41_eq, comparator_42_eq, comparator_43_eq, comparator_44_eq,
       comparator_45_eq, comparator_46_eq, comparator_47_eq, comparator_48_eq, comparator_49_eq,
       comparator_50_eq, comparator_51_eq, comparator_52_eq, comparator_53_eq, comparator_54_eq,
       comparator_55_eq, comparator_56_eq, comparator_57_eq, comparator_58_eq, comparator_59_eq,
       comparator_60_eq, comparator_61_eq, comparator_62_eq, comparator_63_eq, comparator_64_eq,
       comparator_65_eq, comparator_66_eq, comparator_67_eq, comparator_68_eq, comparator_69_eq,
       comparator_70_eq, comparator_71_eq, comparator_72_eq, comparator_73_eq, comparator_74_eq,
       comparator_75_eq, comparator_76_eq, comparator_77_eq, comparator_78_eq, comparator_79_eq,
       comparator_80_eq, comparator_81_eq, is_add, is_addi, is_and, is_andi, is_auipc, is_beq, is_bge,
       is_bgeu, is_blt, is_bltu, is_bne, is_jal, is_jalr, is_lb, is_lh, is_lui, is_lw, is_mul, is_mulh,
       is_mulhu, is_or, is_ori, is_sb, is_sh, is_sll, is_slli, is_slt, is_slti, is_sra, is_srai, is_srl,
       is_srli, is_sub, is_sw, is_xor, is_xori, not_1_out, not_2_out, not_3_out;
  wire [5:0] ROM_IN;
  wire [15:14] rom_1_data;

  ROM #(.addrWidth(6), .dataWidth(16)) rom_1 (
    .addr(ROM_IN), .data({rom_1_data, WBSel, MemWEn, ALUSel, BSel, ASel, BrUn, ImmSel, RegWEn}));
  Comparator #(.mode("unsigned"), .width(7)) comparator_1 (
    .a(Instruction[6:0]), .b(7'b0010011), .eq(comparator_1_eq));  // open: gt, lt
  Comparator #(.mode("unsigned"), .width(3)) comparator_2 (
    .a(Instruction[14:12]), .b(3'b000), .eq(comparator_2_eq));  // open: gt, lt
  Comparator #(.mode("unsigned"), .width(7)) comparator_3 (
    .a(Instruction[6:0]), .b(7'b0010011), .eq(comparator_3_eq));  // open: gt, lt
  Comparator #(.mode("unsigned"), .width(3)) comparator_4 (
    .a(Instruction[14:12]), .b(3'b001), .eq(comparator_4_eq));  // open: gt, lt
  Comparator #(.mode("unsigned"), .width(7)) comparator_5 (
    .a(Instruction[31:25]), .b({7{1'b0}}), .eq(comparator_5_eq));  // open: gt, lt
  Comparator #(.mode("unsigned"), .width(7)) comparator_6 (
    .a(Instruction[6:0]), .b(7'b0010011), .eq(comparator_6_eq));  // open: gt, lt
  Comparator #(.mode("unsigned"), .width(3)) comparator_7 (
    .a(Instruction[14:12]), .b(3'b010), .eq(comparator_7_eq));  // open: gt, lt
  Comparator #(.mode("unsigned"), .width(7)) comparator_8 (
    .a(Instruction[6:0]), .b(7'b0110011), .eq(comparator_8_eq));  // open: gt, lt
  Comparator #(.mode("unsigned"), .width(3)) comparator_9 (
    .a(Instruction[14:12]), .b(3'b000), .eq(comparator_9_eq));  // open: gt, lt
  Comparator #(.mode("unsigned"), .width(7)) comparator_10 (
    .a(Instruction[31:25]), .b({7{1'b0}}), .eq(comparator_10_eq));  // open: gt, lt
  Comparator #(.mode("unsigned"), .width(7)) comparator_11 (
    .a(Instruction[6:0]), .b(7'b0110011), .eq(comparator_11_eq));  // open: gt, lt
  Comparator #(.mode("unsigned"), .width(3)) comparator_12 (
    .a(Instruction[14:12]), .b(3'b000), .eq(comparator_12_eq));  // open: gt, lt
  Comparator #(.mode("unsigned"), .width(7)) comparator_13 (
    .a(Instruction[31:25]), .b(7'b0000001), .eq(comparator_13_eq));  // open: gt, lt
  Comparator #(.mode("unsigned"), .width(7)) comparator_14 (
    .a(Instruction[6:0]), .b(7'b0110011), .eq(comparator_14_eq));  // open: gt, lt
  Comparator #(.mode("unsigned"), .width(3)) comparator_15 (
    .a(Instruction[14:12]), .b(3'b000), .eq(comparator_15_eq));  // open: gt, lt
  Comparator #(.mode("unsigned"), .width(7)) comparator_16 (
    .a(Instruction[31:25]), .b(7'b0100000), .eq(comparator_16_eq));  // open: gt, lt
  Comparator #(.mode("unsigned"), .width(7)) comparator_17 (
    .a(Instruction[6:0]), .b(7'b0110011), .eq(comparator_17_eq));  // open: gt, lt
  Comparator #(.mode("unsigned"), .width(3)) comparator_18 (
    .a(Instruction[14:12]), .b(3'b001), .eq(comparator_18_eq));  // open: gt, lt
  Comparator #(.mode("unsigned"), .width(7)) comparator_19 (
    .a(Instruction[31:25]), .b({7{1'b0}}), .eq(comparator_19_eq));  // open: gt, lt
  and and_1 (is_addi, comparator_1_eq, comparator_2_eq);
  and and_2 (and_2_out, comparator_3_eq, comparator_4_eq);
  and and_3 (is_slti, comparator_6_eq, comparator_7_eq);
  and and_4 (and_4_out, comparator_8_eq, comparator_9_eq);
  and and_5 (and_5_out, comparator_11_eq, comparator_12_eq);
  and and_6 (and_6_out, comparator_14_eq, comparator_15_eq);
  and and_7 (and_7_out, comparator_17_eq, comparator_18_eq);
  // Priority_Encoder #(.select_enc(6)) priority_encoder_1: pin names not known; wires that end beside it: is_xor, is_srl, is_sra, is_or, is_and, is_lb, is_lh, is_lw, is_addi, is_slli, is_slti, is_xori, is_srli, is_srai, is_ori, is_andi, is_sb, is_sh, is_sw, is_beq, is_bne, is_blt, is_bge, is_bltu, ROM_IN, is_bgeu, is_auipc, is_lui, is_jal, is_jalr
  and and_8 (is_slli, and_2_out, comparator_5_eq);
  and and_9 (is_add, and_4_out, comparator_10_eq);
  and and_10 (is_mul, and_5_out, comparator_13_eq);
  and and_11 (is_sub, and_6_out, comparator_16_eq);
  and and_12 (is_sll, and_7_out, comparator_19_eq);
  Comparator #(.mode("unsigned"), .width(7)) comparator_20 (
    .a(Instruction[6:0]), .b(7'b0010011), .eq(comparator_20_eq));  // open: gt, lt
  Comparator #(.mode("unsigned"), .width(3)) comparator_21 (
    .a(Instruction[14:12]), .b(3'b100), .eq(comparator_21_eq));  // open: gt, lt
  Comparator #(.mode("unsigned"), .width(7)) comparator_22 (
    .a(Instruction[6:0]), .b(7'b0010011), .eq(comparator_22_eq));  // open: gt, lt
  Comparator #(.mode("unsigned"), .width(3)) comparator_23 (
    .a(Instruction[14:12]), .b(3'b101), .eq(comparator_23_eq));  // open: gt, lt
  Comparator #(.mode("unsigned"), .width(7)) comparator_24 (
    .a(Instruction[31:25]), .b({7{1'b0}}), .eq(comparator_24_eq));  // open: gt, lt
  Comparator #(.mode("unsigned"), .width(7)) comparator_25 (
    .a(Instruction[6:0]), .b(7'b0010011), .eq(comparator_25_eq));  // open: gt, lt
  Comparator #(.mode("unsigned"), .width(3)) comparator_26 (
    .a(Instruction[14:12]), .b(3'b101), .eq(comparator_26_eq));  // open: gt, lt
  Comparator #(.mode("unsigned"), .width(7)) comparator_27 (
    .a(Instruction[31:25]), .b(7'b0100000), .eq(comparator_27_eq));  // open: gt, lt
  Comparator #(.mode("unsigned"), .width(7)) comparator_28 (
    .a(Instruction[6:0]), .b(7'b0110011), .eq(comparator_28_eq));  // open: gt, lt
  Comparator #(.mode("unsigned"), .width(3)) comparator_29 (
    .a(Instruction[14:12]), .b(3'b001), .eq(comparator_29_eq));  // open: gt, lt
  Comparator #(.mode("unsigned"), .width(7)) comparator_30 (
    .a(Instruction[31:25]), .b(7'b0000001), .eq(comparator_30_eq));  // open: gt, lt
  Comparator #(.mode("unsigned"), .width(7)) comparator_31 (
    .a(Instruction[6:0]), .b(7'b0110011), .eq(comparator_31_eq));  // open: gt, lt
  Comparator #(.mode("unsigned"), .width(3)) comparator_32 (
    .a(Instruction[14:12]), .b(3'b011), .eq(comparator_32_eq));  // open: gt, lt
  Comparator #(.mode("unsigned"), .width(7)) comparator_33 (
    .a(Instruction[31:25]), .b(7'b0000001), .eq(comparator_33_eq));  // open: gt, lt
  Comparator #(.mode("unsigned"), .width(7)) comparator_34 (
    .a(Instruction[6:0]), .b(7'b0110011), .eq(comparator_34_eq));  // open: gt, lt
  Comparator #(.mode("unsigned"), .width(3)) comparator_35 (
    .a(Instruction[14:12]), .b(3'b010), .eq(comparator_35_eq));  // open: gt, lt
  Comparator #(.mode("unsigned"), .width(7)) comparator_36 (
    .a(Instruction[31:25]), .b({7{1'b0}}), .eq(comparator_36_eq));  // open: gt, lt
  Comparator #(.mode("unsigned"), .width(7)) comparator_37 (
    .a(Instruction[6:0]), .b(7'b0110011), .eq(comparator_37_eq));  // open: gt, lt
  Comparator #(.mode("unsigned"), .width(3)) comparator_38 (
    .a(Instruction[14:12]), .b(3'b100), .eq(comparator_38_eq));  // open: gt, lt
  Comparator #(.mode("unsigned"), .width(7)) comparator_39 (
    .a(Instruction[31:25]), .b({7{1'b0}}), .eq(comparator_39_eq));  // open: gt, lt
  and and_13 (is_xori, comparator_20_eq, comparator_21_eq);
  and and_14 (and_14_out, comparator_22_eq, comparator_23_eq);
  and and_15 (and_15_out, comparator_25_eq, comparator_26_eq);
  and and_16 (and_16_out, comparator_28_eq, comparator_29_eq);
  and and_17 (and_17_out, comparator_31_eq, comparator_32_eq);
  and and_18 (and_18_out, comparator_34_eq, comparator_35_eq);
  and and_19 (and_19_out, comparator_37_eq, comparator_38_eq);
  and and_20 (is_srli, and_14_out, comparator_24_eq);
  and and_21 (is_srai, and_15_out, comparator_27_eq);
  and and_22 (is_mulh, and_16_out, comparator_30_eq);
  and and_23 (is_mulhu, and_17_out, comparator_33_eq);
  and and_24 (is_slt, and_18_out, comparator_36_eq);
  and and_25 (is_xor, and_19_out, comparator_39_eq);
  Comparator #(.mode("unsigned"), .width(7)) comparator_40 (
    .a(Instruction[6:0]), .b(7'b0010011), .eq(comparator_40_eq));  // open: gt, lt
  Comparator #(.mode("unsigned"), .width(3)) comparator_41 (
    .a(Instruction[14:12]), .b(3'b110), .eq(comparator_41_eq));  // open: gt, lt
  Comparator #(.mode("unsigned"), .width(7)) comparator_42 (
    .a(Instruction[6:0]), .b(7'b0010011), .eq(comparator_42_eq));  // open: gt, lt
  Comparator #(.mode("unsigned"), .width(3)) comparator_43 (
    .a(Instruction[14:12]), .b(3'b111), .eq(comparator_43_eq));  // open: gt, lt
  Comparator #(.mode("unsigned"), .width(7)) comparator_44 (
    .a(Instruction[6:0]), .b(7'b0110011), .eq(comparator_44_eq));  // open: gt, lt
  Comparator #(.mode("unsigned"), .width(3)) comparator_45 (
    .a(Instruction[14:12]), .b(3'b101), .eq(comparator_45_eq));  // open: gt, lt
  Comparator #(.mode("unsigned"), .width(7)) comparator_46 (
    .a(Instruction[31:25]), .b({7{1'b0}}), .eq(comparator_46_eq));  // open: gt, lt
  Comparator #(.mode("unsigned"), .width(7)) comparator_47 (
    .a(Instruction[6:0]), .b(7'b0110011), .eq(comparator_47_eq));  // open: gt, lt
  Comparator #(.mode("unsigned"), .width(3)) comparator_48 (
    .a(Instruction[14:12]), .b(3'b101), .eq(comparator_48_eq));  // open: gt, lt
  Comparator #(.mode("unsigned"), .width(7)) comparator_49 (
    .a(Instruction[31:25]), .b(7'b0100000), .eq(comparator_49_eq));  // open: gt, lt
  Comparator #(.mode("unsigned"), .width(7)) comparator_50 (
    .a(Instruction[6:0]), .b(7'b0110011), .eq(comparator_50_eq));  // open: gt, lt
  Comparator #(.mode("unsigned"), .width(3)) comparator_51 (
    .a(Instruction[14:12]), .b(3'b110), .eq(comparator_51_eq));  // open: gt, lt
  Comparator #(.mode("unsigned"), .width(7)) comparator_52 (
    .a(Instruction[31:25]), .b({7{1'b0}}), .eq(comparator_52_eq));  // open: gt, lt
  Comparator #(.mode("unsigned"), .width(7)) comparator_53 (
    .a(Instruction[6:0]), .b(7'b0110011), .eq(comparator_53_eq));  // open: gt, lt
  Comparator #(.mode("unsigned"), .width(3)) comparator_54 (
    .a(Instruction[14:12]), .b(3'b111), .eq(comparator_54_eq));  // open: gt, lt
  Comparator #(.mode("unsigned"), .width(7)) comparator_55 (
    .a(Instruction[31:25]), .b({7{1'b0}}), .eq(comparator_55_eq));  // open: gt, lt
  not not_1 (not_1_out, BrLt);
  not not_2 (not_2_out, BrLt);
  not not_3 (not_3_out, BrEq);
  and and_26 (is_ori, comparator_40_eq, comparator_41_eq);
  and and_27 (is_andi, comparator_42_eq, comparator_43_eq);
  and and_28 (and_28_out, comparator_44_eq, comparator_45_eq);
  and and_29 (is_srl, and_28_out, comparator_46_eq);
  and and_30 (and_30_out, comparator_47_eq, comparator_48_eq);
  and and_31 (is_sra, and_30_out, comparator_49_eq);
  and and_32 (and_32_out, comparator_50_eq, comparator_51_eq);
  and and_33 (is_or, and_32_out, comparator_52_eq);
  and and_34 (and_34_out, comparator_53_eq, comparator_54_eq);
  and and_35 (is_and, and_34_out, comparator_55_eq);
  and and_36 (and_36_out, is_beq, BrEq);
  and and_37 (and_37_out, is_bge, not_1_out);
  and and_38 (and_38_out, is_bgeu, not_2_out);
  and and_39 (and_39_out, is_blt, BrLt);
  and and_40 (and_40_out, is_bltu, BrLt);
  and and_41 (and_41_out, is_bne, not_3_out);
  Comparator #(.mode("unsigned"), .width(7)) comparator_56 (
    .a(Instruction[6:0]), .b(7'b0000011), .eq(comparator_56_eq));  // open: gt, lt
  Comparator #(.mode("unsigned"), .width(3)) comparator_57 (
    .a(Instruction[14:12]), .b(3'b000), .eq(comparator_57_eq));  // open: gt, lt
  Comparator #(.mode("unsigned"), .width(7)) comparator_58 (
    .a(Instruction[6:0]), .b(7'b0000011), .eq(comparator_58_eq));  // open: gt, lt
  Comparator #(.mode("unsigned"), .width(3)) comparator_59 (
    .a(Instruction[14:12]), .b(3'b001), .eq(comparator_59_eq));  // open: gt, lt
  Comparator #(.mode("unsigned"), .width(7)) comparator_60 (
    .a(Instruction[6:0]), .b(7'b0000011), .eq(comparator_60_eq));  // open: gt, lt
  Comparator #(.mode("unsigned"), .width(3)) comparator_61 (
    .a(Instruction[14:12]), .b(3'b010), .eq(comparator_61_eq));  // open: gt, lt
  Comparator #(.mode("unsigned"), .width(7)) comparator_62 (
    .a(Instruction[6:0]), .b(7'b1100111), .eq(comparator_62_eq));  // open: gt, lt
  Comparator #(.mode("unsigned"), .width(3)) comparator_63 (
    .a(Instruction[14:12]), .b(3'b000), .eq(comparator_63_eq));  // open: gt, lt
  or or_1 (PCSel, and_36_out, and_37_out, and_38_out, and_39_out, and_40_out, and_41_out, is_jal, is_jalr);
  and and_42 (is_lb, comparator_56_eq, comparator_57_eq);
  and and_43 (is_lh, comparator_58_eq, comparator_59_eq);
  and and_44 (is_lw, comparator_60_eq, comparator_61_eq);
  and and_45 (is_jalr, comparator_62_eq, comparator_63_eq);
  Comparator #(.mode("unsigned"), .width(7)) comparator_64 (
    .a(Instruction[6:0]), .b(7'b1100011), .eq(comparator_64_eq));  // open: gt, lt
  Comparator #(.mode("unsigned"), .width(3)) comparator_65 (
    .a(Instruction[14:12]), .b(3'b000), .eq(comparator_65_eq));  // open: gt, lt
  Comparator #(.mode("unsigned"), .width(7)) comparator_66 (
    .a(Instruction[6:0]), .b(7'b1100011), .eq(comparator_66_eq));  // open: gt, lt
  Comparator #(.mode("unsigned"), .width(3)) comparator_67 (
    .a(Instruction[14:12]), .b(3'b001), .eq(comparator_67_eq));  // open: gt, lt
  Comparator #(.mode("unsigned"), .width(7)) comparator_68 (
    .a(Instruction[6:0]), .b(7'b1100011), .eq(comparator_68_eq));  // open: gt, lt
  Comparator #(.mode("unsigned"), .width(3)) comparator_69 (
    .a(Instruction[14:12]), .b(3'b100), .eq(comparator_69_eq));  // open: gt, lt
  Comparator #(.mode("unsigned"), .width(7)) comparator_70 (
    .a(Instruction[6:0]), .b(7'b1100011), .eq(comparator_70_eq));  // open: gt, lt
  Comparator #(.mode("unsigned"), .width(3)) comparator_71 (
    .a(Instruction[14:12]), .b(3'b101), .eq(comparator_71_eq));  // open: gt, lt
  Comparator #(.mode("unsigned"), .width(7)) comparator_72 (
    .a(Instruction[6:0]), .b(7'b0100011), .eq(comparator_72_eq));  // open: gt, lt
  Comparator #(.mode("unsigned"), .width(3)) comparator_73 (
    .a(Instruction[14:12]), .b(3'b000), .eq(comparator_73_eq));  // open: gt, lt
  Comparator #(.mode("unsigned"), .width(7)) comparator_74 (
    .a(Instruction[6:0]), .b(7'b0100011), .eq(comparator_74_eq));  // open: gt, lt
  Comparator #(.mode("unsigned"), .width(3)) comparator_75 (
    .a(Instruction[14:12]), .b(3'b001), .eq(comparator_75_eq));  // open: gt, lt
  Comparator #(.mode("unsigned"), .width(7)) comparator_76 (
    .a(Instruction[6:0]), .b(7'b0100011), .eq(comparator_76_eq));  // open: gt, lt
  Comparator #(.mode("unsigned"), .width(3)) comparator_77 (
    .a(Instruction[14:12]), .b(3'b010), .eq(comparator_77_eq));  // open: gt, lt
  and and_46 (is_beq, comparator_64_eq, comparator_65_eq);
  and and_47 (is_bne, comparator_66_eq, comparator_67_eq);
  and and_48 (is_blt, comparator_68_eq, comparator_69_eq);
  and and_49 (is_bge, comparator_70_eq, comparator_71_eq);
  and and_50 (is_sb, comparator_72_eq, comparator_73_eq);
  and and_51 (is_sh, comparator_74_eq, comparator_75_eq);
  and and_52 (is_sw, comparator_76_eq, comparator_77_eq);
  Comparator #(.mode("unsigned"), .width(7)) comparator_78 (
    .a(Instruction[6:0]), .b(7'b1100011), .eq(comparator_78_eq));  // open: gt, lt
  Comparator #(.mode("unsigned"), .width(3)) comparator_79 (
    .a(Instruction[14:12]), .b(3'b110), .eq(comparator_79_eq));  // open: gt, lt
  Comparator #(.mode("unsigned"), .width(7)) comparator_80 (
    .a(Instruction[6:0]), .b(7'b1100011), .eq(comparator_80_eq));  // open: gt, lt
  Comparator #(.mode("unsigned"), .width(3)) comparator_81 (
    .a(Instruction[14:12]), .b(3'b111), .eq(comparator_81_eq));  // open: gt, lt
  Comparator #(.mode("unsigned"), .width(7)) comparator_82 (
    .a(Instruction[6:0]), .b(7'b0010111), .eq(is_auipc));  // open: gt, lt
  Comparator #(.mode("unsigned"), .width(7)) comparator_83 (
    .a(Instruction[6:0]), .b(7'b0110111), .eq(is_lui));  // open: gt, lt
  and and_53 (is_bltu, comparator_78_eq, comparator_79_eq);
  and and_54 (is_bgeu, comparator_80_eq, comparator_81_eq);
  Comparator #(.mode("unsigned"), .width(7)) comparator_84 (
    .a(Instruction[6:0]), .b(7'b1101111), .eq(is_jal));  // open: gt, lt

  // Other names for the same wires on the sheet: opcode[6:0] = Instruction[6:0]; funct3[2:0] = Instruction[14:12];
  //   funct7[6:0] = Instruction[31:25]

  // Notes on the sheet:
  //   Connect ROM Input here ->
  //   INPUTS to your circuit
  //   contents of rom_1 (hex, n*v repeats v):
  //   1001 1401 1601 1081 1481 1581 1101 1201 1281 1681 1301 1381 41 41 41 1041 10c1 1141 1241 12c1 16c1
  //   1341 13c1 1842 1842 1842 4*1064 1074 1074 1067 17c7 2069 2041
  //   ROM FOR CONTROL LOGIC
  //   I-Format
  //   R-Format
  //   DON'T CHANGE THE LOCATIONS OF THE INPUTS AND OUTPUTS!
  //   This is only if you choose to do the ROM option
  //   CONNECT
  //   WIRE
  //   TO
  //   USE
  //   ROM
  //   OUTPUT from your circuit
  //   Reminder: If using ROM, use combinational logic for PCSel
  //   B-Format
  //   S-Format
  //   U-Format
  //   J-Format
endmodule
