// Logisim project cpu.circ as structural Verilog: 1 circuit, main circuit cpu
module cpu (
  input  clk,
  input  [31:0] Instruction,
  input  [31:0] MemReadData,
  output [31:0] MemAddress,
  output [31:0] ProgramCounter,
  output [31:0] ra,
  output [31:0] sp,
  output [31:0] t0,
  output [31:0] t1,
  output [31:0] t2,
  output [31:0] s0,
  output [31:0] s1,
  output [31:0] a0,
  output [3:0] MemWriteMask,
  output [31:0] MemWriteData
);

  wire ASel, BrEq, BrLt, BrUn, BSel, MemWEn, PCSel, RegWEn;
  wire [1:0] WBSel;
  wire [2:0] ImmSel;
  wire [3:0] ALUSel;
  wire [31:0] adder_1_out, DataToReg, Immediate, InputA, InputB, Instruction_ex, multiplexer_1_out,
       multiplexer_2_out, multiplexer_3_out, ProgramCounter_ex, RegReadData1, RegReadData2;

  Adder #(.width(32)) adder_1 (.a(ProgramCounter), .b(32'h4), .out(adder_1_out));  // open: cin, cout
  Multiplexer #(.width(32)) multiplexer_1 (.in0(adder_1_out), .in1(MemAddress), .out(multiplexer_1_out), .sel(PCSel));
  Register #(.width(32)) PC (.D(multiplexer_1_out), .clk(clk), .Q(ProgramCounter));  // open: en, clr
  Register #(.width(32)) PC_ex (.D(ProgramCounter), .clk(clk), .Q(ProgramCounter_ex));  // open: en, clr
  Register #(.width(32)) u_Instruction_ex (.D(multiplexer_2_out), .clk(clk), .Q(Instruction_ex));  // open: en, clr
  Multiplexer #(.width(32)) multiplexer_2 (.in0(Instruction), .in1(32'h13), .out(multiplexer_2_out), .sel(PCSel));
  Multiplexer #(.select(2), .width(32)) multiplexer_3 (
    .in0(DataToReg), .in1(MemAddress), .in2(ProgramCounter), .out(multiplexer_3_out), .sel(WBSel));  // open: in3
  control_logic control_logic_1 (
    .PCSel(PCSel), .RegWEn(RegWEn), .ImmSel(ImmSel), .BrUn(BrUn), .ASel(ASel), .BSel(BSel), .ALUSel(ALUSel),
    .MemWEn(MemWEn), .WBSel(WBSel), .Instruction(Instruction_ex), .BrEq(BrEq), .BrLt(BrLt));
  regfile regfile_1 (
    .ReadReg1(Instruction_ex[19:15]), .ReadReg2(Instruction_ex[24:20]), .WriteReg(Instruction_ex[11:7]),
    .RegWriteData(multiplexer_3_out), .RegWEn(RegWEn), .clk(clk), .ra(ra), .sp(sp), .t0(t0), .t1(t1),
    .t2(t2), .s0(s0), .s1(s1), .a0(a0), .RegReadData1(RegReadData1), .RegReadData2(RegReadData2));
  imm_gen imm_gen_1 (.Instruction(Instruction_ex), .ImmSel(ImmSel), .Immediate(Immediate));
  Multiplexer #(.width(32)) multiplexer_4 (.in0(RegReadData1), .in1(ProgramCounter_ex), .out(InputA), .sel(ASel));
  Multiplexer #(.width(32)) multiplexer_5 (.in0(RegReadData2), .in1(Immediate), .out(InputB), .sel(BSel));
  alu alu_1 (.ALUResult(MemAddress), .A(InputA), .B(InputB), .ALUSel(ALUSel));
  branch_comp branch_comp_1 (.BrData1(RegReadData1), .BrData2(RegReadData2), .BrUn(BrUn), .BrEq(BrEq), .BrLt(BrLt));
  partial_store partial_store_1 (
    .Instruction(Instruction_ex), .MemAddress(MemAddress), .DataFromReg(RegReadData2), .MemWEn(MemWEn),
    .MemWriteMask(MemWriteMask), .DataToMem(MemWriteData));
  partial_load partial_load_1 (
    .Instruction(Instruction_ex), .MemAddress(MemAddress), .DataFromMem(MemReadData), .DataToReg(DataToReg));

  // Other names for the same wires on the sheet: ALUResult[31:0] = MemAddress; WriteReg[4:0] = Instruction_ex[11:7];
  //   ReadReg1[4:0] = Instruction_ex[19:15]; ReadReg2[4:0] = Instruction_ex[24:20]

  // Notes on the sheet:
  //   To IMEM
  //   IMEM (do **NOT** move this)
  //   From IMEM
  //   Inputs/Outputs for testing. Do **NOT** move these.
  //   It is OK to move the PC, RegFile, ALU, MEM, Branch Comp, Imm Gen, Partial Load, Partial Store and Control Logic to wherever is most convenient for you when constructing your CPU, and to delete this text
  //   To DMEM
  //   DMEM (do **NOT** move this)
  //   From DMEM
endmodule
