// Logisim project regfile.circ as structural Verilog: 1 circuit, main circuit regfile
module regfile (
  input  [4:0] ReadReg1,
  input  [4:0] ReadReg2,
  input  [4:0] WriteReg,
  input  [31:0] RegWriteData,
  input  RegWEn,
  input  clk,
  output [31:0] ra,
  output [31:0] sp,
  output [31:0] t0,
  output [31:0] t1,
  output [31:0] t2,
  output [31:0] s0,
  output [31:0] s1,
  output [31:0] a0,
  output [31:0] RegReadData1,
  output [31:0] RegReadData2
);

  wire w0, w1, w2, w3, w4, w5, w6, w7, w8, w9, w10, w11, w12, w13, w14, w15, w16, w17, w18, w19, w20, w21,
       w22, w23, w24, w25, w26, w27, w28, w29, w30, w31;
  wire [31:0] q3, q4, q11, q12, q13, q14, q15, q16, q17, q18, q19, q20, q21, q22, q23, q24, q25, q26, q27,
       q28, q29, q30, q31;

  Register #(.width(32)) register_1 (.D(RegWriteData), .en(w1), .clk(clk), .Q(ra));  // open: clr
  Register #(.width(32)) register_2 (.D(RegWriteData), .en(w2), .clk(clk), .Q(sp));  // open: clr
  Register #(.width(32)) register_3 (.D(RegWriteData), .en(w3), .clk(clk), .Q(q3));  // open: clr
  Register #(.width(32)) register_4 (.D(RegWriteData), .en(w4), .clk(clk), .Q(q4));  // open: clr
  Register #(.width(32)) register_5 (.D(RegWriteData), .en(w5), .clk(clk), .Q(t0));  // open: clr
  Register #(.width(32)) register_6 (.D(RegWriteData), .en(w6), .clk(clk), .Q(t1));  // open: clr
  Register #(.width(32)) register_7 (.D(RegWriteData), .en(w7), .clk(clk), .Q(t2));  // open: clr
  Register #(.width(32)) register_8 (.D(RegWriteData), .en(w8), .clk(clk), .Q(s0));  // open: clr
  Register #(.width(32)) register_9 (.D(RegWriteData), .en(w9), .clk(clk), .Q(s1));  // open: clr
  Register #(.width(32)) register_10 (.D(RegWriteData), .en(w10), .clk(clk), .Q(a0));  // open: clr
  Register #(.width(32)) register_11 (.D(RegWriteData), .en(w11), .clk(clk), .Q(q11));  // open: clr
  Register #(.width(32)) register_12 (.D(RegWriteData), .en(w12), .clk(clk), .Q(q12));  // open: clr
  Register #(.width(32)) register_13 (.D(RegWriteData), .en(w13), .clk(clk), .Q(q13));  // open: clr
  Register #(.width(32)) register_14 (.D(RegWriteData), .en(w14), .clk(clk), .Q(q14));  // open: clr
  Register #(.width(32)) register_15 (.D(RegWriteData), .en(w15), .clk(clk), .Q(q15));  // open: clr
  Demultiplexer #(.select(5)) demultiplexer_1 (
    .out0(w0), .out1(w1), .out2(w2), .out3(w3), .out4(w4), .out5(w5), .out6(w6), .out7(w7), .out8(w8),
    .out9(w9), .out10(w10), .out11(w11), .out12(w12), .out13(w13), .out14(w14), .out15(w15), .out16(w16),
    .out17(w17), .out18(w18), .out19(w19), .out20(w20), .out21(w21), .out22(w22), .out23(w23), .out24(w24),
    .out25(w25), .out26(w26), .out27(w27), .out28(w28), .out29(w29), .out30(w30), .out31(w31), .in(RegWEn),
    .sel(WriteReg));
  Multiplexer #(.select(5), .width(32)) multiplexer_1 (
    .in0({32{1'b0}}), .in1(ra), .in2(sp), .in3(q3), .in4(q4), .in5(t0), .in6(t1), .in7(t2), .in8(s0),
    .in9(s1), .in10(a0), .in11(q11), .in12(q12), .in13(q13), .in14(q14), .in15(q15), .in16(q16), .in17(q17),
    .in18(q18), .in19(q19), .in20(q20), .in21(q21), .in22(q22), .in23(q23), .in24(q24), .in25(q25),
    .in26(q26), .in27(q27), .in28(q28), .in29(q29), .in30(q30), .in31(q31), .out(RegReadData1), .sel(ReadReg1));
  Multiplexer #(.select(5), .width(32)) multiplexer_2 (
    .in0({32{1'b0}}), .in1(ra), .in2(sp), .in3(q3), .in4(q4), .in5(t0), .in6(t1), .in7(t2), .in8(s0),
    .in9(s1), .in10(a0), .in11(q11), .in12(q12), .in13(q13), .in14(q14), .in15(q15), .in16(q16), .in17(q17),
    .in18(q18), .in19(q19), .in20(q20), .in21(q21), .in22(q22), .in23(q23), .in24(q24), .in25(q25),
    .in26(q26), .in27(q27), .in28(q28), .in29(q29), .in30(q30), .in31(q31), .out(RegReadData2), .sel(ReadReg2));
  Register #(.width(32)) register_16 (.D(RegWriteData), .en(w16), .clk(clk), .Q(q16));  // open: clr
  Register #(.width(32)) register_17 (.D(RegWriteData), .en(w17), .clk(clk), .Q(q17));  // open: clr
  Register #(.width(32)) register_18 (.D(RegWriteData), .en(w18), .clk(clk), .Q(q18));  // open: clr
  Register #(.width(32)) register_19 (.D(RegWriteData), .en(w19), .clk(clk), .Q(q19));  // open: clr
  Register #(.width(32)) register_20 (.D(RegWriteData), .en(w20), .clk(clk), .Q(q20));  // open: clr
  Register #(.width(32)) register_21 (.D(RegWriteData), .en(w21), .clk(clk), .Q(q21));  // open: clr
  Register #(.width(32)) register_22 (.D(RegWriteData), .en(w22), .clk(clk), .Q(q22));  // open: clr
  Register #(.width(32)) register_23 (.D(RegWriteData), .en(w22), .clk(clk), .Q(q22));  // open: clr
  Register #(.width(32)) register_24 (.D(RegWriteData), .en(w23), .clk(clk), .Q(q23));  // open: clr
  Register #(.width(32)) register_25 (.D(RegWriteData), .en(w24), .clk(clk), .Q(q24));  // open: clr
  Register #(.width(32)) register_26 (.D(RegWriteData), .en(w25), .clk(clk), .Q(q25));  // open: clr
  Register #(.width(32)) register_27 (.D(RegWriteData), .en(w26), .clk(clk), .Q(q26));  // open: clr
  Register #(.width(32)) register_28 (.D(RegWriteData), .en(w27), .clk(clk), .Q(q27));  // open: clr
  Register #(.width(32)) register_29 (.D(RegWriteData), .en(w28), .clk(clk), .Q(q28));  // open: clr
  Register #(.width(32)) register_30 (.D(RegWriteData), .en(w29), .clk(clk), .Q(q29));  // open: clr
  Register #(.width(32)) register_31 (.D(RegWriteData), .en(w30), .clk(clk), .Q(q30));  // open: clr
  Register #(.width(32)) register_32 (.D(RegWriteData), .en(w31), .clk(clk), .Q(q31));  // open: clr

  // Notes on the sheet:
  //   INPUTS to your circuit
  //   DON'T CHANGE THE LOCATIONS OF THE INPUTS AND OUTPUTS!
  //   These are DEBUG/TEST outputs from your circuit.
  //   OUTPUTS from your circuit
endmodule
